# Fritzing sketch OpenMQTTgateway_Arduino_Addon_IR (saved by Fritzing 0.9.3b)
breadboards: 1

parts:
  V1 = DC Power [voltage=5]
  LED2 = LEDs [package=led10mm]
  R2 = Resistor [tolerance=±5% resistance=330 package="2512 [SMD]"]
  Q1 = TRANSISTOR_NPN [package=to-92-ammo]
  IR2 = TSOP312.., 314.. [package=THT]
  Bauteil1 = Arduino Uno (Rev3)

nets:
  N1: V1.V+, LED2.C, IR2.Vs, Bauteil1.5V
  N2: LED2.A, Q1.C
  N3: R2.Pin_0, Q1.B
  N4: R2.Pin_1, Bauteil1.D9_PWM
  GND: Q1.E, IR2.GND, Bauteil1.GND
  N5: IR2.Data, Bauteil1.D3_PWM
